# Fritzing sketch tilt_debounced (saved by Fritzing 1.0.3b)
breadboards: 1

parts:
  R1 = Resistor [tolerance=±5% power=0.25W resistance=470 package=THT]
  Part1 = Arduino Uno (Rev3) - ICSP
  NEOPIXEL1 = Neopixel Strip -- Black (30/m) [part_number=1376]
  C1 = Electrolytic Capacitor [capacitance=10μF voltage=35V package="0605 [SMD, electrolytic]"]
  JACK1 = 2.1mm Barrel Jack with Terminal Block
  S1 = Tilt Switch [package=THT]

nets:
  N1: R1.Pin_0, NEOPIXEL1.Din
  N2: R1.Pin_1, Part1.D3_PWM
  GND: Part1.GND, NEOPIXEL1.GND, C1.-, JACK1.NEG, S1.Pin_2
  N3: Part1.D2, S1.Pin_1
  VIN: Part1.VIN, NEOPIXEL1.+5V, C1.+, JACK1.POS

custom parts:
  Neopixel Strip -- Black (30/m): These NeoPixel strips have 30 digitally-addressable pixel LEDs per meter and are very affordable and are only 12.5 mm wide, 10 mm if you remove the strip from the casing.

// code stored in the sketch: Untitled5.ino
void setup(){
Serial.begin(9600);
}

void loop(){
Serial.println("Hello World");

}
